# Fritzing sketch Project Sketch (saved by Fritzing 0.9.3b)
breadboards: 1

parts:
  Part1 = Arduino Uno (Rev3) - ICSP  # not connected
  Part2 = Rotoshield - Motor driver shield for Arduino
  VCC1 = Battery
  M1 = DC Motor
  M2 = DC Motor
  Part3 = Bluetooth HC-05 Macho
  R1 = Resistor [tolerance=±5% resistance=220 package=THT]
  R2 = Resistor [tolerance=±5% resistance=220 package=THT]
  R3 = Resistor [tolerance=±5% resistance=220 package=THT]

nets:
  N1: Part2.DIG_0, Part3.TXD
  N2: Part2.DIG_1, R3.Pin_1
  +5V: Part2.+5V, Part3.VCC
  GND: Part2.GND, VCC1.-, Part3.GND, R2.Pin_0
  N3: Part2.M1-2, M2.pin_2
  N4: Part2.M1-1, M2.pin_1
  N5: Part2.M4-2, M1.pin_2
  N6: Part2.M4-1, M1.pin_1
  N7: Part2.VCC, VCC1.+
  N8: Part3.RXD, R1.Pin_1, R3.Pin_0
  N9: R1.Pin_0, R2.Pin_1

// code stored in the sketch: Bluetooth_RC_Car.ino
/* 
 *  Bluetooth RC Car
 *  An arduino based RC car that makes use of the arduino motor shield and HC-06 bluetooth module
 *  Aaditya Sondhi
*/


#include <AFMotor.h> //Motor shield library

AF_DCMotor motorR(1); //Right motor setup
AF_DCMotor motorL(4); //Left motor setup

void setup() {
  Serial.begin(9600); //Setup serial comminication
  Serial.println("RC Car by Aaditya Sondhi");

  // turn on motors
  motorL.setSpeed(255);
  motorR.setSpeed(255);
  motorL.run(RELEASE);
  motorR.run(RELEASE);
}

void loop() {
  
   if(Serial.available() > 0)
  {
    char data;
    data = Serial.read();
    Serial.write(Serial.read());
   
    switch (data)
    {
      case '1': //FORWARD
        motorL.run(FORWARD);
        motorL.setSpeed(255);    
        motorR.run(FORWARD);
        motorR.setSpeed(255);
        break;
      case '2': //REVERSE
        motorL.run(BACKWARD);
        motorL.setSpeed(255);    
        motorR.run(BACKWARD);
        motorR.setSpeed(255);
        break;
      case '3': //FORWARD LEFT
        motorR.run(FORWARD);
        motorR.setSpeed(255);
        break;
      case '4': //FORWARD RIGHT
        motorL.run(FORWARD);
        motorL.setSpeed(255);
        break;
      case '5': //REVERSE LEFT
        motorL.run(BACKWARD);
        motorL.setSpeed(255);
        break;
      case '6': //REVERSE RIGHT
        motorR.run(BACKWARD);
        motorR.setSpeed(255);
        break;
      default: //If bluetooth module receives any value not listed above, both motors turn off
        motorL.run(RELEASE);
        motorR.run(RELEASE);
    }

    
  }
 
 
}
